# Fritzing sketch MotoAlarm (saved by Fritzing 0.9.6b)
breadboards: 1

parts:
  M1 = RioRand LM2596
  C1 = Electrolytic Capacitor [capacitance=1000µF voltage=35V package="300 mil [THT, electrolytic]"]
  Part1 = InvenSense MPU6050
  Part2 = Arduino Nano (Rev3.0)
  SIM800L_BO1 = SIM800L BO
  Power_plug1 = Power plug

nets:
  N1: M1.Pin_1, Power_plug1.VCC
  GND: M1.Pin_2, Part1.GND, Power_plug1.GND
  N2: M1.Pin_3, C1.+, SIM800L_BO1.PIN2
  N3: M1.Pin_4, C1.-, SIM800L_BO1.pin_6
  VCC: Part1.VCC, Part2.3V3
  N4: Part1.SCL, Part2.A4
  N5: Part1.SDA, Part2.A3
  N6: Part2.D2, SIM800L_BO1.pin_4
  N7: Part2.D3, SIM800L_BO1.pin_5

notes:
  Converter lowers the voltage on the SIM800L module to ~4V
